# Fritzing sketch door (saved by Fritzing 0.9.3b)
breadboards: 1

parts:
  Part1 = Arduino Nano (Rev3.0)
  R1 = Resistor [tolerance=±5% resistance=220 package="0805 [SMD]"]
  BAT1 = BC9VPC [package=bc9vpc]
  S1 = Reed switch [package=THT]

nets:
  N1: Part1.GND, R1.Pin_0, BAT1.V-
  N2: Part1.D2, R1.Pin_1, S1.pin_2
  N3: Part1.VIN, BAT1.V+
  N4: Part1.3V3, S1.pin_1
